// Logisim project branch-comp.circ as structural Verilog: 1 circuit, main circuit branch_comp
module branch_comp (
  input  [31:0] BrData1,
  input  [31:0] BrData2,
  input  BrUn,
  output BrEq,
  output BrLt
);

  wire comparator_2_eq, comparator_2_lt, mux1, mux2;

  Comparator #(.width(32)) comparator_1 (.a(BrData1), .b(BrData2), .eq(mux1), .lt(mux2));  // open: gt
  Comparator #(.mode("unsigned"), .width(32)) comparator_2 (
    .a(BrData1), .b(BrData2), .eq(comparator_2_eq), .lt(comparator_2_lt));  // open: gt
  Multiplexer multiplexer_1 (.in0(mux2), .in1(comparator_2_lt), .out(BrLt), .sel(BrUn));
  Multiplexer multiplexer_2 (.in0(mux1), .in1(comparator_2_eq), .out(BrEq), .sel(BrUn));

  // Notes on the sheet:
  //   INPUTS to your circuit
  //   DON'T CHANGE THE LOCATIONS OF THE INPUTS AND OUTPUTS!
  //   OUTPUT from your circuit
endmodule
