// Logisim project control-logic.circ as structural Verilog: 1 circuit, main circuit control_logic
module control_logic (
  input  [31:0] Instruction,
  input  BrEq,
  input  BrLt,
  output PCSel,
  output RegWEn,
  output [2:0] ImmSel,
  output BrUn,
  output ASel,
  output BSel,
  output [3:0] ALUSel,
  output MemWEn,
  output [1:0] WBSel
);

  wire als, ALU, B, cc, comparator_1_eq, comparator_2_eq, comparator_3_eq, comparator_4_eq, comparator_5_eq,
       comparator_6_eq, comparator_7_eq, comparator_8_eq, comparator_9_eq, comparator_10_eq,
       comparator_11_eq, comparator_14_eq, comparator_15_eq, comparator_17_eq, comparator_18_eq,
       comparator_19_eq, comparator_21_eq, comparator_22_eq, comparator_23_eq, comparator_25_eq,
       comparator_26_eq, comparator_27_eq, comparator_28_eq, comparator_29_eq, comparator_30_eq,
       comparator_31_eq, comparator_32_eq, comparator_33_eq, comparator_34_eq, comparator_35_eq,
       comparator_36_eq, comparator_37_eq, comparator_38_eq, comparator_39_eq, comparator_40_eq,
       comparator_41_eq, comparator_42_eq, comparator_43_eq, comparator_44_eq, comparator_45_eq,
       comparator_46_eq, comparator_47_eq, comparator_48_eq, comparator_49_eq, comparator_50_eq,
       comparator_51_eq, comparator_52_eq, comparator_53_eq, comparator_54_eq, comparator_55_eq,
       comparator_56_eq, comparator_57_eq, comparator_58_eq, comparator_59_eq, comparator_60_eq,
       comparator_61_eq, comparator_62_eq, J, lui2, mul2, mulh2, nand_1_out, nand_2_out, nand_3_out,
       nand_4_out, nand_9_out, nand_10_out, nand_11_out, nand_12_out, nand_13_out, nand_14_out, nand_15_out,
       nand_16_out, nand_17_out, nand_18_out, nand_19_out, nand_20_out, nor_1_out, nor_3_out, nor_4_out,
       nor_6_out, nor_7_out, nor_8_out, nor_9_out, nor_10_out, nor_11_out, nor_12_out, nor_14_out,
       nor_17_out, nor_18_out, nor_21_out, nor_22_out, nor_23_out, nor_24_out, nor_25_out, not_1_out,
       not_2_out, not_3_out, S, sra2, sub2, U;
  wire [1:0] N4;
  wire [2:0] N1, N2, N3;
  wire [3:0] alusel_t, hey, hey1, hey2, hey3, hey4;
  wire [5:0] undriven;
  wire [15:0] rom_1_data;

  Comparator #(.width(7)) comparator_1 (.a(Instruction[31:25]), .b(7'b0000001), .eq(comparator_1_eq));  // open: gt, lt
  Comparator #(.width(3)) comparator_2 (.a(Instruction[14:12]), .b(3'b000), .eq(comparator_2_eq));  // open: gt, lt
  Comparator #(.width(7)) comparator_3 (.a(Instruction[6:0]), .b(7'b0110011), .eq(comparator_3_eq));  // open: gt, lt
  Multiplexer #(.width(4)) multiplexer_1 (.in0(hey1), .in1(4'b1001), .out(hey2), .sel(mulh2));
  Multiplexer #(.width(4)) multiplexer_2 (.in0(hey2), .in1(4'b1100), .out(hey3), .sel(sub2));
  Comparator #(.width(7)) comparator_4 (.a(Instruction[31:25]), .b(7'b0000001), .eq(comparator_4_eq));  // open: gt, lt
  Comparator #(.width(3)) comparator_5 (.a(Instruction[14:12]), .b(3'b001), .eq(comparator_5_eq));  // open: gt, lt
  Comparator #(.width(7)) comparator_6 (.a(Instruction[6:0]), .b(7'b0110011), .eq(comparator_6_eq));  // open: gt, lt
  Comparator #(.width(7)) comparator_7 (.a(Instruction[31:25]), .b(7'b0100000), .eq(comparator_7_eq));  // open: gt, lt
  Comparator #(.width(3)) comparator_8 (.a(Instruction[14:12]), .b(3'b000), .eq(comparator_8_eq));  // open: gt, lt
  Comparator #(.width(7)) comparator_9 (.a(Instruction[6:0]), .b(7'b0110011), .eq(comparator_9_eq));  // open: gt, lt
  Comparator #(.width(7)) comparator_10 (
    .a(Instruction[31:25]), .b(7'b0100000), .eq(comparator_10_eq));  // open: gt, lt
  Comparator #(.width(3)) comparator_11 (.a(Instruction[14:12]), .b(3'b101), .eq(comparator_11_eq));  // open: gt, lt
  Multiplexer #(.width(4)) multiplexer_3 (.in0(hey), .in1(4'b1000), .out(hey1), .sel(mul2));
  Multiplexer #(.width(4)) multiplexer_4 (.in0(hey3), .in1(4'b1101), .out(hey4), .sel(sra2));
  ROM #(.addrWidth(6), .dataWidth(16)) rom_1 (.addr(undriven), .data(rom_1_data));
  nand nand_1 (nand_1_out, comparator_1_eq, comparator_2_eq, comparator_3_eq);
  nand nand_2 (nand_2_out, comparator_4_eq, comparator_5_eq, comparator_6_eq);
  nand nand_3 (nand_3_out, comparator_7_eq, comparator_8_eq, comparator_9_eq);
  nand nand_4 (nand_4_out, comparator_10_eq, comparator_11_eq);
  Comparator #(.width(7)) comparator_12 (.a(Instruction[6:0]), .b(7'b0100011), .eq(S));  // open: gt, lt
  Comparator #(.width(7)) comparator_13 (.a(Instruction[6:0]), .b(7'b1100011), .eq(B));  // open: gt, lt
  Comparator #(.width(7)) comparator_14 (.a(Instruction[6:0]), .b(7'b0010111), .eq(comparator_14_eq));  // open: gt, lt
  Comparator #(.width(7)) comparator_15 (.a(Instruction[6:0]), .b(7'b0110111), .eq(comparator_15_eq));  // open: gt, lt
  Comparator #(.width(7)) comparator_16 (.a(Instruction[6:0]), .b(7'b1101111), .eq(J));  // open: gt, lt
  nand nand_5 (mul2, nand_1_out, nand_1_out);
  nand nand_6 (mulh2, nand_2_out, nand_2_out);
  nand nand_7 (sub2, nand_3_out, nand_3_out);
  nand nand_8 (sra2, nand_4_out, nand_4_out);
  nor nor_1 (nor_1_out, comparator_14_eq, comparator_15_eq);
  Comparator #(.width(7)) comparator_17 (.a(Instruction[6:0]), .b(7'b1100011), .eq(comparator_17_eq));  // open: gt, lt
  Comparator #(.width(7)) comparator_18 (.a(Instruction[6:0]), .b(7'b0010111), .eq(comparator_18_eq));  // open: gt, lt
  Comparator #(.width(7)) comparator_19 (.a(Instruction[6:0]), .b(7'b1101111), .eq(comparator_19_eq));  // open: gt, lt
  Multiplexer #(.width(4)) multiplexer_5 (.in0(hey4), .in1(4'b1111), .out(alusel_t), .sel(lui2));
  nor nor_2 (U, nor_1_out, nor_1_out);
  nor nor_3 (nor_3_out, comparator_17_eq, comparator_18_eq, comparator_19_eq);
  Comparator #(.width(7)) comparator_20 (.a(Instruction[6:0]), .b(7'b0100011), .eq(MemWEn));  // open: gt, lt
  Comparator #(.width(7)) comparator_21 (.a(Instruction[6:0]), .b(7'b1100011), .eq(comparator_21_eq));  // open: gt, lt
  Comparator #(.width(3)) comparator_22 (.a(Instruction[14:12]), .b(3'b110), .eq(comparator_22_eq));  // open: gt, lt
  Comparator #(.width(3)) comparator_23 (.a(Instruction[14:12]), .b(3'b111), .eq(comparator_23_eq));  // open: gt, lt
  Comparator #(.width(7)) comparator_24 (.a(Instruction[6:0]), .b(7'b0110111), .eq(lui2));  // open: gt, lt
  nor nor_4 (nor_4_out, comparator_22_eq, comparator_23_eq);
  nor nor_5 (ASel, nor_3_out, nor_3_out);
  Multiplexer #(.width(4)) multiplexer_6 (.in0(4'b0000), .in1(alusel_t), .out(ALUSel), .sel(als));
  Comparator #(.width(7)) comparator_25 (.a(Instruction[6:0]), .b(7'b0110011), .eq(comparator_25_eq));  // open: gt, lt
  Comparator #(.width(7)) comparator_26 (.a(Instruction[6:0]), .b(7'b0010011), .eq(comparator_26_eq));  // open: gt, lt
  Comparator #(.width(7)) comparator_27 (.a(Instruction[6:0]), .b(7'b0110111), .eq(comparator_27_eq));  // open: gt, lt
  Comparator #(.width(7)) comparator_28 (.a(Instruction[6:0]), .b(7'b0010011), .eq(comparator_28_eq));  // open: gt, lt
  Comparator #(.width(7)) comparator_29 (.a(Instruction[6:0]), .b(7'b0110011), .eq(comparator_29_eq));  // open: gt, lt
  Comparator #(.width(7)) comparator_30 (.a(Instruction[6:0]), .b(7'b0000011), .eq(comparator_30_eq));  // open: gt, lt
  Comparator #(.width(7)) comparator_31 (.a(Instruction[6:0]), .b(7'b1100111), .eq(comparator_31_eq));  // open: gt, lt
  Comparator #(.width(7)) comparator_32 (.a(Instruction[6:0]), .b(7'b1101111), .eq(comparator_32_eq));  // open: gt, lt
  Comparator #(.width(7)) comparator_33 (.a(Instruction[6:0]), .b(7'b0110111), .eq(comparator_33_eq));  // open: gt, lt
  Comparator #(.width(7)) comparator_34 (.a(Instruction[6:0]), .b(7'b0010111), .eq(comparator_34_eq));  // open: gt, lt
  Comparator #(.width(7)) comparator_35 (.a(Instruction[6:0]), .b(7'b0010011), .eq(comparator_35_eq));  // open: gt, lt
  Comparator #(.width(7)) comparator_36 (.a(Instruction[6:0]), .b(7'b1100011), .eq(comparator_36_eq));  // open: gt, lt
  Comparator #(.width(7)) comparator_37 (.a(Instruction[6:0]), .b(7'b0000011), .eq(comparator_37_eq));  // open: gt, lt
  Comparator #(.width(7)) comparator_38 (.a(Instruction[6:0]), .b(7'b0100011), .eq(comparator_38_eq));  // open: gt, lt
  Comparator #(.width(7)) comparator_39 (.a(Instruction[6:0]), .b(7'b1101111), .eq(comparator_39_eq));  // open: gt, lt
  Comparator #(.width(7)) comparator_40 (.a(Instruction[6:0]), .b(7'b1100111), .eq(comparator_40_eq));  // open: gt, lt
  Comparator #(.width(7)) comparator_41 (.a(Instruction[6:0]), .b(7'b0010111), .eq(comparator_41_eq));  // open: gt, lt
  Comparator #(.width(7)) comparator_42 (.a(Instruction[6:0]), .b(7'b0110111), .eq(comparator_42_eq));  // open: gt, lt
  nor nor_6 (nor_6_out, nor_4_out, nor_4_out);
  Multiplexer #(.select(3), .width(4)) multiplexer_7 (
    .in0(4'b0000), .in1(4'b0001), .in2(4'b0010), .in3(4'b1011), .in4(4'b0100), .in5(4'b0101), .in6(4'b0110),
    .in7(4'b0111), .out(hey), .sel(Instruction[14:12]));
  and and_1 (BrUn, comparator_21_eq, nor_6_out);
  nor nor_7 (nor_7_out, comparator_28_eq, comparator_29_eq, comparator_30_eq);
  nor nor_8 (nor_8_out, comparator_32_eq, comparator_33_eq, comparator_34_eq);
  nor nor_9 (nor_9_out, comparator_25_eq, comparator_26_eq, comparator_27_eq);
  nor nor_10 (nor_10_out, nor_7_out, nor_7_out);
  nor nor_11 (nor_11_out, comparator_35_eq, comparator_36_eq, comparator_37_eq, comparator_38_eq, comparator_39_eq, comparator_40_eq, comparator_41_eq, comparator_42_eq);
  Multiplexer #(.width(3)) multiplexer_8 (.in0(3'b000), .in1(3'b001), .out(N1), .sel(S));
  nor nor_12 (nor_12_out, nor_8_out, nor_8_out);
  Multiplexer #(.width(3)) multiplexer_9 (.in0(N1), .in1(3'b010), .out(N2), .sel(B));
  Multiplexer #(.width(2)) multiplexer_10 (.in0(2'b00), .in1(2'b01), .out(N4), .sel(ALU));
  Multiplexer #(.width(2)) multiplexer_11 (.in0(N4), .in1(2'b10), .out(WBSel), .sel(cc));
  nor nor_13 (als, nor_9_out, nor_9_out);
  nor nor_14 (nor_14_out, nor_10_out, comparator_31_eq, nor_12_out);
  nor nor_15 (BSel, nor_11_out, nor_11_out);
  Multiplexer #(.width(3)) multiplexer_12 (.in0(N2), .in1(3'b011), .out(N3), .sel(U));
  Multiplexer #(.width(3)) multiplexer_13 (.in0(N3), .in1(3'b100), .out(ImmSel), .sel(J));
  nor nor_16 (RegWEn, nor_14_out, nor_14_out);
  Comparator #(.width(7)) comparator_43 (.a(Instruction[6:0]), .b(7'b1100011), .eq(comparator_43_eq));  // open: gt, lt
  Comparator #(.width(3)) comparator_44 (.a(Instruction[14:12]), .b(3'b000), .eq(comparator_44_eq));  // open: gt, lt
  Comparator #(.width(7)) comparator_45 (.a(Instruction[6:0]), .b(7'b1100011), .eq(comparator_45_eq));  // open: gt, lt
  Comparator #(.width(3)) comparator_46 (.a(Instruction[14:12]), .b(3'b101), .eq(comparator_46_eq));  // open: gt, lt
  Comparator #(.width(7)) comparator_47 (.a(Instruction[6:0]), .b(7'b1100011), .eq(comparator_47_eq));  // open: gt, lt
  Comparator #(.width(3)) comparator_48 (.a(Instruction[14:12]), .b(3'b111), .eq(comparator_48_eq));  // open: gt, lt
  Comparator #(.width(7)) comparator_49 (.a(Instruction[6:0]), .b(7'b1100011), .eq(comparator_49_eq));  // open: gt, lt
  Comparator #(.width(3)) comparator_50 (.a(Instruction[14:12]), .b(3'b100), .eq(comparator_50_eq));  // open: gt, lt
  Comparator #(.width(7)) comparator_51 (.a(Instruction[6:0]), .b(7'b1100011), .eq(comparator_51_eq));  // open: gt, lt
  Comparator #(.width(3)) comparator_52 (.a(Instruction[14:12]), .b(3'b110), .eq(comparator_52_eq));  // open: gt, lt
  Comparator #(.width(7)) comparator_53 (.a(Instruction[6:0]), .b(7'b1100011), .eq(comparator_53_eq));  // open: gt, lt
  Comparator #(.width(3)) comparator_54 (.a(Instruction[14:12]), .b(3'b001), .eq(comparator_54_eq));  // open: gt, lt
  Comparator #(.width(7)) comparator_55 (.a(Instruction[6:0]), .b(7'b0110011), .eq(comparator_55_eq));  // open: gt, lt
  Comparator #(.width(7)) comparator_56 (.a(Instruction[6:0]), .b(7'b0010111), .eq(comparator_56_eq));  // open: gt, lt
  Comparator #(.width(7)) comparator_57 (.a(Instruction[6:0]), .b(7'b0010011), .eq(comparator_57_eq));  // open: gt, lt
  Comparator #(.width(7)) comparator_58 (.a(Instruction[6:0]), .b(7'b0110111), .eq(comparator_58_eq));  // open: gt, lt
  Comparator #(.width(7)) comparator_59 (.a(Instruction[6:0]), .b(7'b1101111), .eq(comparator_59_eq));  // open: gt, lt
  Comparator #(.width(7)) comparator_60 (.a(Instruction[6:0]), .b(7'b1100111), .eq(comparator_60_eq));  // open: gt, lt
  not not_1 (not_1_out, BrLt);
  not not_2 (not_2_out, BrLt);
  not not_3 (not_3_out, BrEq);
  nor nor_17 (nor_17_out, comparator_55_eq, comparator_56_eq, comparator_57_eq, comparator_58_eq);
  nor nor_18 (nor_18_out, comparator_59_eq, comparator_60_eq);
  nor nor_19 (ALU, nor_17_out, nor_17_out);
  nor nor_20 (cc, nor_18_out, nor_18_out);
  nand nand_9 (nand_9_out, comparator_43_eq, comparator_44_eq, BrEq);
  nand nand_10 (nand_10_out, comparator_45_eq, comparator_46_eq, not_1_out);
  nand nand_11 (nand_11_out, comparator_47_eq, comparator_48_eq, not_2_out);
  nand nand_12 (nand_12_out, comparator_49_eq, comparator_50_eq, BrLt);
  nand nand_13 (nand_13_out, comparator_51_eq, comparator_52_eq, BrLt);
  Comparator #(.width(7)) comparator_61 (.a(Instruction[6:0]), .b(7'b1101111), .eq(comparator_61_eq));  // open: gt, lt
  Comparator #(.width(7)) comparator_62 (.a(Instruction[6:0]), .b(7'b1100111), .eq(comparator_62_eq));  // open: gt, lt
  nand nand_14 (nand_14_out, nand_10_out, nand_10_out);
  nand nand_15 (nand_15_out, nand_11_out, nand_11_out);
  nand nand_16 (nand_16_out, nand_12_out, nand_12_out);
  nand nand_17 (nand_17_out, nand_13_out, nand_13_out);
  nor nor_21 (nor_21_out, comparator_61_eq, comparator_62_eq);
  nand nand_18 (nand_18_out, nand_9_out, nand_9_out);
  nand nand_19 (nand_19_out, comparator_53_eq, comparator_54_eq, not_3_out);
  nand nand_20 (nand_20_out, nand_19_out, nand_19_out);
  nor nor_22 (nor_22_out, nor_21_out, nor_21_out);
  nor nor_23 (nor_23_out, nand_18_out, nand_14_out, nand_15_out, nand_16_out, nand_17_out, nand_20_out);
  nor nor_24 (nor_24_out, nor_23_out, nor_23_out);
  nor nor_25 (nor_25_out, nor_22_out, nor_24_out);
  nor nor_26 (PCSel, nor_25_out, nor_25_out);

  // Other names for the same wires on the sheet: opcode[6:0] = Instruction[6:0]; rd[4:0] = Instruction[11:7];
  //   func3[2:0] = Instruction[14:12]; rs1[4:0] = Instruction[19:15]; rs2[4:0] = Instruction[24:20];
  //   func7[6:0] = Instruction[31:25]

  // Notes on the sheet:
  //   INPUTS to your circuit
  //   Connect ROM Input here ->
  //   ROM FOR CONTROL LOGIC
  //   DON'T CHANGE THE LOCATIONS OF THE INPUTS AND OUTPUTS!
  //   This is only if you choose to do the ROM option
  //   CONNECT
  //   TO
  //   USE
  //   ROM
  //   OUTPUT from your circuit
endmodule
