// Logisim project cpu.circ as structural Verilog: 1 circuit, main circuit cpu
module cpu (
  input  clk,
  input  [31:0] Instruction,
  input  [31:0] MemReadData,
  output [31:0] MemAddress,
  output [31:0] ProgramCounter,
  output [31:0] ra,
  output [31:0] sp,
  output [31:0] t0,
  output [31:0] t1,
  output [31:0] t2,
  output [31:0] s0,
  output [31:0] s1,
  output [31:0] a0,
  output [3:0] MemWriteMask,
  output [31:0] MemWriteData
);

  wire ASel, BrEq, BrLt, BrUn, BSel, MemWEn, PCSel, RegWEn;
  wire [1:0] WBSel;
  wire [2:0] func3, ImmSel;
  wire [3:0] ALUSel;
  wire [6:0] func7;
  wire [24:0] in2;
  wire [31:0] A, adder_1_out, adder_2_out, B, Datareg, imm, multiplexer_1_out, multiplexer_2_out, pc2, reg1,
       reg2, write;

  Adder #(.width(32)) adder_1 (.a(ProgramCounter), .b(32'h4), .out(adder_1_out));  // open: cin, cout
  Multiplexer #(.width(32)) multiplexer_1 (.in0(adder_1_out), .in1(MemAddress), .out(multiplexer_1_out), .sel(PCSel));
  Register #(.width(32)) register_1 (.D(ProgramCounter), .clk(clk), .Q(pc2));  // open: en, clr
  Register #(.width(32)) PC (.D(multiplexer_1_out), .clk(clk), .Q(ProgramCounter));  // open: en, clr
  imm_gen imm_gen_1 (.Instruction({func7, in2[24:15], func3, in2[11:0]}), .ImmSel(ImmSel), .Immediate(imm));
  alu alu_1 (.ALUResult(MemAddress), .A(A), .B(B), .ALUSel(ALUSel));
  control_logic control_logic_1 (
    .PCSel(PCSel), .RegWEn(RegWEn), .ImmSel(ImmSel), .BrUn(BrUn), .ASel(ASel), .BSel(BSel), .ALUSel(ALUSel),
    .MemWEn(MemWEn), .WBSel(WBSel), .Instruction({func7, in2[24:15], func3, in2[11:0]}), .BrEq(BrEq),
    .BrLt(BrLt));
  Register #(.width(32)) register_2 (
    .D(multiplexer_2_out), .clk(clk), .Q({func7, in2[24:15], func3, in2[11:0]}));  // open: en, clr
  Multiplexer #(.width(32)) multiplexer_2 (.in0(Instruction), .in1(32'h13), .out(multiplexer_2_out), .sel(PCSel));
  Multiplexer #(.width(32)) multiplexer_3 (.in0(reg1), .in1(pc2), .out(A), .sel(ASel));
  Multiplexer #(.width(32)) multiplexer_4 (.in0(reg2), .in1(imm), .out(B), .sel(BSel));
  Adder #(.width(32)) adder_2 (.a(pc2), .b(32'h4), .out(adder_2_out));  // open: cin, cout
  branch_comp branch_comp_1 (.BrData1(reg1), .BrData2(reg2), .BrUn(BrUn), .BrEq(BrEq), .BrLt(BrLt));
  Multiplexer #(.select(2), .width(32)) multiplexer_5 (
    .in0(Datareg), .in1(MemAddress), .in2(adder_2_out), .out(write), .sel(WBSel));  // open: in3
  regfile regfile_1 (
    .ReadIndex1(in2[19:15]), .ReadIndex2(in2[24:20]), .WriteIndex(in2[11:7]), .WriteData(write),
    .RegWEn(RegWEn), .clk(clk), .ra(ra), .sp(sp), .t0(t0), .t1(t1), .t2(t2), .s0(s0), .s1(s1), .a0(a0),
    .ReadData1(reg1), .ReadData2(reg2));
  partial_store partial_store_1 (
    .Instruction({func7, in2[24:15], func3, in2[11:0]}), .MemAddress(MemAddress), .DataFromReg(reg2),
    .MemWEn(MemWEn), .MemWriteMask(MemWriteMask), .DataToMem(MemWriteData));
  partial_load partial_load_1 (
    .Instruction({func7, in2[24:15], func3, in2[11:0]}), .MemAddress(MemAddress), .DataFromMem(MemReadData),
    .DataToReg(Datareg));

  // Other names for the same wires on the sheet: opcode[6:0] = in2[6:0]; rd[4:0] = in2[11:7];
  //   in2 (some bits) = {func7, func3}; rs1[4:0] = in2[19:15]; rs2[4:0] = in2[24:20]; o[31:0] = MemAddress

  // Notes on the sheet:
  //   To IMEM
  //   IMEM (do **NOT** move this)
  //   From IMEM
  //   Inputs/Outputs for testing. Do **NOT** move these.
  //   It is OK to move the PC, RegFile, ALU, MEM, Branch Comp, Imm Gen, Partial Load, Partial Store and Control Logic to wherever is most convenient for you when constructing your CPU, and to delete this text
  //   To DMEM
  //   DMEM (do **NOT** move this)
  //   From DMEM
endmodule
