// Logisim project partial-load.circ as structural Verilog: 1 circuit, main circuit partial_load
module partial_load (
  input  [31:0] Instruction,
  input  [31:0] MemAddress,
  input  [31:0] DataFromMem,
  output [31:0] DataToReg
);

  wire [7:0] conn;
  wire [15:0] conn1;
  wire [31:0] bit_extender_1_out, bit_extender_2_out;

  BitSelector #(.group(8), .width(32)) bitselector_1 (.in(DataFromMem), .out(conn), .sel(MemAddress[1:0]));
  Multiplexer #(.select(2), .width(16)) multiplexer_1 (
    .in0(DataFromMem[15:0]), .in1(DataFromMem[23:8]), .in2(DataFromMem[31:16]), .out(conn1),
    .sel(MemAddress[1:0]));  // open: in3
  assign bit_extender_1_out = {{24{conn[7]}}, conn};  // Bit_Extender bit_extender_1
  assign bit_extender_2_out = {{16{conn1[15]}}, conn1};  // Bit_Extender bit_extender_2
  Multiplexer #(.select(2), .width(32)) multiplexer_2 (
    .in0(bit_extender_1_out), .in1(bit_extender_2_out), .in2(DataFromMem), .out(DataToReg),
    .sel(Instruction[13:12]));  // open: in3

  // Other names for the same wires on the sheet: opcode[6:0] = Instruction[6:0]; rd[4:0] = Instruction[11:7];
  //   func3[2:0] = Instruction[14:12]; rs1[4:0] = Instruction[19:15]; rs2[4:0] = Instruction[24:20];
  //   func7[6:0] = Instruction[31:25]

  // Notes on the sheet:
  //   INPUTS to your circuit
  //   DON'T CHANGE THE LOCATIONS OF THE INPUTS AND OUTPUTS!
  //   OUTPUT from your circuit
endmodule
