// Logisim project partial-store.circ as structural Verilog: 1 circuit, main circuit partial_store
module partial_store (
  input  [31:0] Instruction,
  input  [31:0] MemAddress,
  input  [31:0] DataFromReg,
  input  MemWEn,
  output [3:0] MemWriteMask,
  output [31:0] DataToMem
);

  wire [1:0] bit_extender_1_out, bit_extender_2_out;
  wire [3:0] hi2, Hl;
  wire [31:0] A, B;

  Multiplexer #(.select(2), .width(4)) multiplexer_1 (
    .in0(4'b0001), .in1(4'b0011), .in2(4'b1111), .out(Hl), .sel(Instruction[13:12]));  // open: in3
  Multiplexer #(.select(2), .width(4)) multiplexer_2 (
    .in0(4'b0100), .in1(4'b1100), .out(hi2), .sel(Instruction[13:12]));  // open: in2, in3
  Multiplexer #(.enable("true"), .select(2), .width(4)) multiplexer_3 (
    .in0(Hl), .in1(4'b0010), .in2(hi2), .in3(4'b1000), .out(MemWriteMask), .sel(MemAddress[1:0]), .en(MemWEn));
  Bit_Extender #(.in_width(32), .out_width(2)) bit_extender_1 (.in(MemAddress), .out(bit_extender_1_out));
  Bit_Extender #(.in_width(32), .out_width(2)) bit_extender_2 (.in(MemAddress), .out(bit_extender_2_out));
  Multiplexer #(.enable("true"), .select(2), .width(32)) multiplexer_4 (
    .in0(A), .in1(B), .in2(DataFromReg), .out(DataToMem), .sel(Instruction[13:12]), .en(MemWEn));  // open: in3
  Multiplexer #(.select(2), .width(32)) multiplexer_5 (
    .in0({{24{1'b0}}, DataFromReg[7:0]}), .in1({{16{1'b0}}, DataFromReg[7:0], {8{1'b0}}}),
    .in2({{8{1'b0}}, DataFromReg[7:0], {16{1'b0}}}), .in3({DataFromReg[7:0], {24{1'b0}}}), .out(A),
    .sel(bit_extender_2_out));
  Multiplexer #(.select(2), .width(32)) multiplexer_6 (
    .in0({{16{1'b0}}, DataFromReg[15:0]}), .in2({DataFromReg[15:0], {16{1'b0}}}), .out(B),
    .sel(bit_extender_1_out));  // open: in1, in3

  // Other names for the same wires on the sheet: C = MemWEn; opcode[6:0] = Instruction[6:0];
  //   rd[4:0] = Instruction[11:7]; func3[2:0] = Instruction[14:12]; rs1[4:0] = Instruction[19:15];
  //   rs2[4:0] = Instruction[24:20]; func7[6:0] = Instruction[31:25]

  // Notes on the sheet:
  //   INPUTS to your circuit
  //   DON'T CHANGE THE LOCATIONS OF THE INPUTS AND OUTPUTS!
  //   OUTPUT from your circuit
endmodule
