// Logisim project regfile.circ as structural Verilog: 1 circuit, main circuit regfile
module regfile (
  input  [4:0] ReadIndex1,
  input  [4:0] ReadIndex2,
  input  [4:0] WriteIndex,
  input  [31:0] WriteData,
  input  RegWEn,
  input  clk,
  output [31:0] ra,
  output [31:0] sp,
  output [31:0] t0,
  output [31:0] t1,
  output [31:0] t2,
  output [31:0] s0,
  output [31:0] s1,
  output [31:0] a0,
  output [31:0] ReadData1,
  output [31:0] ReadData2
);

  wire wen1, wen2, wen3, wen4, wen5, wen6, wen7, wen8, wen9, wen10, wen11, wen12, wen13, wen14, wen15, wen16,
       wen17, wen18, wen19, wen20, wen21, wen22, wen23, wen24, wen25, wen26, wen27, wen28, wen29, wen30,
       wen31;
  wire [31:0] i0, i3, i4, i11, i12, i13, i14, i15, i16, i17, i18, i19, i20, i21, i22, i23, i24, i25, i26,
       i27, i28, i29, i30, i31;

  Register #(.width(32)) register_1 (.D(WriteData), .en(wen1), .clk(clk), .Q(ra));  // open: clr
  Register #(.width(32)) register_2 (.D({32{1'b0}}), .clk(clk), .Q(i0));  // open: en, clr
  Register #(.width(32)) register_3 (.D(WriteData), .en(wen1), .clk(clk), .Q(ra));  // open: clr
  Register #(.width(32)) register_4 (.D(WriteData), .en(wen2), .clk(clk), .Q(sp));  // open: clr
  Register #(.width(32)) register_5 (.D(WriteData), .en(wen3), .clk(clk), .Q(i3));  // open: clr
  Register #(.width(32)) register_6 (.D(WriteData), .en(wen4), .clk(clk), .Q(i4));  // open: clr
  Register #(.width(32)) register_7 (.D(WriteData), .en(wen5), .clk(clk), .Q(t0));  // open: clr
  Register #(.width(32)) register_8 (.D(WriteData), .en(wen6), .clk(clk), .Q(t1));  // open: clr
  Register #(.width(32)) register_9 (.D(WriteData), .en(wen7), .clk(clk), .Q(t2));  // open: clr
  Register #(.width(32)) register_10 (.D(WriteData), .en(wen8), .clk(clk), .Q(s0));  // open: clr
  Register #(.width(32)) register_11 (.D(WriteData), .en(wen9), .clk(clk), .Q(s1));  // open: clr
  Register #(.width(32)) register_12 (.D(WriteData), .en(wen10), .clk(clk), .Q(a0));  // open: clr
  Register #(.width(32)) register_13 (.D(WriteData), .en(wen11), .clk(clk), .Q(i11));  // open: clr
  Register #(.width(32)) register_14 (.D(WriteData), .en(wen12), .clk(clk), .Q(i12));  // open: clr
  Register #(.width(32)) register_15 (.D(WriteData), .en(wen13), .clk(clk), .Q(i13));  // open: clr
  Register #(.width(32)) register_16 (.D(WriteData), .en(wen14), .clk(clk), .Q(i14));  // open: clr
  Register #(.width(32)) register_17 (.D(WriteData), .en(wen15), .clk(clk), .Q(i15));  // open: clr
  Register #(.width(32)) register_18 (.D(WriteData), .en(wen16), .clk(clk), .Q(i16));  // open: clr
  Register #(.width(32)) register_19 (.D(WriteData), .en(wen17), .clk(clk), .Q(i17));  // open: clr
  Register #(.width(32)) register_20 (.D(WriteData), .en(wen18), .clk(clk), .Q(i18));  // open: clr
  Register #(.width(32)) register_21 (.D(WriteData), .en(wen19), .clk(clk), .Q(i19));  // open: clr
  Register #(.width(32)) register_22 (.D(WriteData), .en(wen2), .clk(clk), .Q(sp));  // open: clr
  Register #(.width(32)) register_23 (.D(WriteData), .en(wen20), .clk(clk), .Q(i20));  // open: clr
  Register #(.width(32)) register_24 (.D(WriteData), .en(wen21), .clk(clk), .Q(i21));  // open: clr
  Register #(.width(32)) register_25 (.D(WriteData), .en(wen22), .clk(clk), .Q(i22));  // open: clr
  Register #(.width(32)) register_26 (.D(WriteData), .en(wen23), .clk(clk), .Q(i23));  // open: clr
  Register #(.width(32)) register_27 (.D(WriteData), .en(wen24), .clk(clk), .Q(i24));  // open: clr
  Register #(.width(32)) register_28 (.D(WriteData), .en(wen25), .clk(clk), .Q(i25));  // open: clr
  Register #(.width(32)) register_29 (.D(WriteData), .en(wen26), .clk(clk), .Q(i26));  // open: clr
  Register #(.width(32)) register_30 (.D(WriteData), .en(wen27), .clk(clk), .Q(i27));  // open: clr
  Register #(.width(32)) register_31 (.D(WriteData), .en(wen28), .clk(clk), .Q(i28));  // open: clr
  Register #(.width(32)) register_32 (.D(WriteData), .en(wen29), .clk(clk), .Q(i29));  // open: clr
  Register #(.width(32)) register_33 (.D(WriteData), .en(wen30), .clk(clk), .Q(i30));  // open: clr
  Register #(.width(32)) register_34 (.D(WriteData), .en(wen31), .clk(clk), .Q(i31));  // open: clr
  Multiplexer #(.select(5), .width(32)) multiplexer_1 (
    .in0(i0), .in1(ra), .in2(sp), .in3(i3), .in4(i4), .in5(t0), .in6(t1), .in7(t2), .in8(s0), .in9(s1),
    .in10(a0), .in11(i11), .in12(i12), .in13(i13), .in14(i14), .in15(i15), .in16(i16), .in17(i17),
    .in18(i18), .in19(i19), .in20(i20), .in21(i21), .in22(i22), .in23(i23), .in24(i24), .in25(i25),
    .in26(i26), .in27(i27), .in28(i28), .in29(i29), .in30(i30), .in31(i31), .out(ReadData1), .sel(ReadIndex1));
  Demultiplexer #(.select(5)) demultiplexer_1 (
    .out1(wen1), .out2(wen2), .out3(wen3), .out4(wen4), .out5(wen5), .out6(wen6), .out7(wen7), .out8(wen8),
    .out9(wen9), .out10(wen10), .out11(wen11), .out12(wen12), .out13(wen13), .out14(wen14), .out15(wen15),
    .out16(wen16), .out17(wen17), .out18(wen18), .out19(wen19), .out20(wen20), .out21(wen21), .out22(wen22),
    .out23(wen23), .out24(wen24), .out25(wen25), .out26(wen26), .out27(wen27), .out28(wen28), .out29(wen29),
    .out30(wen30), .out31(wen31), .in(RegWEn), .sel(WriteIndex));  // open: out0
  Multiplexer #(.select(5), .width(32)) multiplexer_2 (
    .in0(i0), .in1(ra), .in2(sp), .in3(i3), .in4(i4), .in5(t0), .in6(t1), .in7(t2), .in8(s0), .in9(s1),
    .in10(a0), .in11(i11), .in12(i12), .in13(i13), .in14(i14), .in15(i15), .in16(i16), .in17(i17),
    .in18(i18), .in19(i19), .in20(i20), .in21(i21), .in22(i22), .in23(i23), .in24(i24), .in25(i25),
    .in26(i26), .in27(i27), .in28(i28), .in29(i29), .in30(i30), .in31(i31), .out(ReadData2), .sel(ReadIndex2));

  // Other names for the same wires on the sheet: i1[31:0] = ra; i2[31:0] = sp; i5[31:0] = t0; i6[31:0] = t1;
  //   i7[31:0] = t2; i8[31:0] = s0; i9[31:0] = s1; i10[31:0] = a0

  // Notes on the sheet:
  //   INPUTS to your circuit
  //   DON'T CHANGE THE LOCATIONS OF THE INPUTS AND OUTPUTS!
  //   These are DEBUG/TEST outputs from your circuit.
  //   OUTPUTS from your circuit
endmodule
